# Fritzing sketch blinkyEonMonCube (saved by Fritzing 0.9.10b)
breadboards: 1

parts:
  BT1 = Bluetooth HC-06u [package=THT]
  Teensy_LC1 = Teensy-LC
  R1 = Resistor [tolerance=±5% power=0.25 resistance=10k package=THT]
  J1 = RJ11 Jack [package=rj11-6]

nets:
  VCC: BT1.VCC, Teensy_LC1.Vin, J1.2
  GND: BT1.GND, Teensy_LC1.GND, J1.3, J1.6
  N1: BT1.TXD, Teensy_LC1.D9
  N2: BT1.RXD, Teensy_LC1.D8
  N3: Teensy_LC1.D0, R1.Pin_1, J1.5
  N4: Teensy_LC1.D12, Teensy_LC1.5Vout
  N5: Teensy_LC1.Program, Teensy_LC1.A12/DAC, Teensy_LC1.D13
  N6: Teensy_LC1.A7/D21, Teensy_LC1.A11
  N7: Teensy_LC1.A8/D22, Teensy_LC1.A10
  N8: Teensy_LC1.A9/D23, Teensy_LC1.AREF
  N9: Teensy_LC1.3V3, R1.Pin_0
  N10: Teensy_LC1.AGND, Teensy_LC1.VUSB

notes:
  6
  5
  3
  2

custom parts:
  Bluetooth HC-06u: Bluetooth HC-06 - face up, pins down 16.5mm x 37.5mm PCB
  Teensy-LC: Teensy-LC (Low Cost) is a powerful 32 bit microcontroller board, with a rich set of hardware peripherals, at a very affordable price! Teensy-LC delivers an impressive collection of capabilities to make modern electronic projects simpler. It features an ARM Cortex-M0+ processor at 48 MHz, 62K Flash, 8K RAM, 12 bit analog input & output, hardware Serial, SPI & I2C, USB, and a total of 27 I/O pins.
